// Digital circuit unidad_aritmetica_logica.dig as structural Verilog
module unidad_aritmetica_logica (
  input  invB,
  input  logica,
  input  \and ,
  input  [15:0] A,
  input  [15:0] B,
  output [15:0] R
);

  wire [15:0] add_1_s, and_1_out, multiplexer_1_out, not_1_out, or_1_out;

  assign not_1_out = ~B;  // Not not_1, 16 bits wide
  Multiplexer #(.Bits(16)) multiplexer_1 (.sel(invB), .in_0(B), .in_1(not_1_out), .out(multiplexer_1_out));
  Add #(.Bits(16)) add_1 (.a(A), .b(multiplexer_1_out), .c_i(invB), .s(add_1_s));  // open: c_o
  assign or_1_out = A | multiplexer_1_out;  // Or or_1, 16 bits wide
  assign and_1_out = A & multiplexer_1_out;  // And and_1, 16 bits wide
  Multiplexer #(.Selector_Bits(3), .Bits(16)) multiplexer_2 (
    .sel({invB, logica, \and }), .in_0(add_1_s), .in_1(add_1_s), .in_2(or_1_out), .in_3(and_1_out),
    .in_4(add_1_s), .in_5(add_1_s), .in_6(or_1_out), .in_7(and_1_out), .out(R));
endmodule
